# Fritzing sketch Circuit (saved by Fritzing 0.9.10b)

parts:
  Part1 = Adafruit TCS34725 RGB Color Sensor [part_number="Adafruit #1334"]
  Mod1 = Raspberry Pi 4B
  VCC2 = 4 x AAA Battery Mount
  J1 = Basic Servo
  J2 = Basic Servo

nets:
  VIN: Part1.VIN, Mod1.5V
  GND: Part1.GND, Mod1.GND, VCC2.-
  N1: Part1.SCL, Mod1.GPIO3
  N2: Part1.SDA, Mod1.GPIO2
  N3: Part1.LED_EN, Mod1.3V3
  N4: Mod1.GPIO12, J1.pulse
  N5: Mod1.GPIO13, J2.pulse

custom parts:
  Adafruit TCS34725 RGB Color Sensor: Your electronics can now see in dazzling color with this lovely color light sensor. We found the best color sensor on the market, the TCS34725, which has RGB and Clear light sensing elements. An IR blocking filter, integrated on-chip and localized to the color sensing photodiodes, minimizes the IR spectral component of the incoming light and allows color measurements to be made accurately. The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
